// Logisim project cpu1.circ as structural Verilog: 1 circuit, main circuit main
module main (
);

  wire and_1_out, and_2_out, and_3_out, and_4_out, and_5_out, and_6_out, and_7_out, and_8_out, and_9_out,
       and_10_out, and_11_out, and_12_out, and_13_out, and_14_out, and_15_out, and_16_out, and_17_out,
       and_18_out, and_19_out, and_20_out, and_21_out, and_22_out, and_23_out, and_24_out, and_25_out,
       and_26_out, and_27_out, and_28_out, and_29_out, and_30_out, and_31_out, and_32_out, and_33_out,
       and_34_out, and_35_out, and_36_out, and_37_out, and_38_out, and_39_out, and_40_out, and_41_out,
       and_42_out, and_43_out, and_44_out, and_45_out, and_46_out, and_47_out, and_48_out, and_49_out,
       and_50_out, and_51_out, and_52_out, and_53_out, and_54_out, and_55_out, and_56_out, and_57_out,
       and_58_out, and_59_out, carry1_out, carry2_out, carry3_out, carry4_out, carry5_out, carry6_out,
       carry7_out, carry8_out, carry9_out, carry10_out, carry11_out, carry12_out, carry13_out, carry14_out,
       carry15_out, clc_out, controlled_buffer_1_out, cpy_out, from_alu0_out, from_alu1_out, from_alu2_out,
       from_out0_out, from_reg1_out, from_reg2_out, from_reg3_out, from_reg4_out, from_reg5_out,
       from_reg6_out, gto_out, hlt_out, imm_out, main_sys_clock_out, multiplexer_1_out, not_1_out, not_2_out,
       not_3_out, not_4_out, not_5_out, not_6_out, not_7_out, not_8_out, not_9_out, not_10_out, not_11_out,
       not_12_out, not_13_out, not_14_out, not_15_out, not_16_out, not_17_out, not_18_out, not_19_out,
       not_20_out, not_21_out, not_22_out, not_23_out, not_24_out, not_25_out, not_26_out, not_27_out,
       not_28_out, not_29_out, not_30_out, not_31_out, not_32_out, not_33_out, not_34_out, not_35_out,
       not_36_out, not_37_out, not_38_out, not_39_out, not_40_out, not_41_out, not_42_out, not_43_out,
       not_44_out, not_45_out, not_46_out, not_47_out, not_48_out, not_49_out, not_50_out, not_51_out,
       not_52_out, not_53_out, not_54_out, not_55_out, not_56_out, not_57_out, not_58_out, not_59_out,
       not_60_out, not_61_out, not_62_out, not_63_out, not_64_out, not_65_out, not_66_out, not_67_out,
       not_68_out, not_69_out, not_70_out, not_71_out, not_72_out, not_73_out, not_74_out, not_75_out,
       not_76_out, not_77_out, not_78_out, not_79_out, not_80_out, not_81_out, not_82_out, not_83_out,
       not_84_out, not_85_out, not_86_out, not_87_out, not_88_out, not_89_out, not_90_out, not_91_out,
       not_92_out, not_93_out, not_94_out, not_95_out, not_96_out, not_97_out, not_98_out, not_99_out,
       not_100_out, not_101_out, not_102_out, not_103_out, not_104_out, not_105_out, not_106_out,
       not_107_out, not_108_out, not_109_out, or_1_out, rst_out, to_alu0_out, to_alu1_out, to_alu2_out,
       to_out0_out, to_reg0_out, to_reg1_out, to_reg2_out, to_reg3_out, to_reg4_out, to_reg5_out,
       to_reg6_out, xor_1_out, xor_2_out, xor_3_out, xor_4_out, xor_5_out, xor_6_out, xor_7_out, xor_8_out,
       xor_9_out, xor_10_out, xor_11_out, xor_12_out, xor_13_out, xor_14_out, xor_15_out, xor_16_out;
  wire [3:0] or_2_out;
  wire [11:0] counter_1_q;
  wire [15:0] alu0_q, alu1_q, alu2_q, and_60_out, bit1_out, multiplexer_2_out, multiplexer_3_out,
       multiplexer_4_out, multiplexer_5_out, nand_1_out, nor_1_out, or_6_out, out0_q, reg0_q, reg1_q, reg2_q,
       reg3_q, reg4_q, reg5_q, reg6_q, rom_1_data;

  Clock main_sys_clock (.out(main_sys_clock_out));
  assign controlled_buffer_1_out = not_1_out ? main_sys_clock_out : 1'bz;  // Controlled_Buffer controlled_buffer_1
  not not_1 (not_1_out, hlt_out);
  Counter #(.max('hfff), .width(12)) counter_1 (
    .clr(rst_out), .load(gto_out), .clk(controlled_buffer_1_out), .D(rom_1_data[11:0]), .Q(counter_1_q));  // open: up, count, carry
  ROM #(.addrWidth(12), .dataWidth(16)) rom_1 (.addr(counter_1_q), .data(rom_1_data));
  not not_2 (not_2_out, rom_1_data[12]);
  not not_3 (not_3_out, rom_1_data[13]);
  not not_4 (not_4_out, rom_1_data[14]);
  not not_5 (not_5_out, rom_1_data[15]);
  not not_6 (not_6_out, rom_1_data[13]);
  and imm (imm_out, not_2_out, not_3_out, not_4_out, not_5_out);
  and cpy (cpy_out, rom_1_data[12], not_6_out, not_7_out, not_8_out);
  Multiplexer #(.enable("true")) multiplexer_1 (
    .in0(imm_out), .in1(and_1_out), .out(multiplexer_1_out), .sel(cpy_out));  // open: en
  not not_7 (not_7_out, rom_1_data[14]);
  not not_8 (not_8_out, rom_1_data[15]);
  not not_9 (not_9_out, rom_1_data[12]);
  not not_10 (not_10_out, rom_1_data[14]);
  not not_11 (not_11_out, rom_1_data[15]);
  not not_12 (not_12_out, rom_1_data[12]);
  and clc (clc_out, not_9_out, rom_1_data[13], not_10_out, not_11_out);
  not not_13 (not_13_out, rom_1_data[5]);
  not not_14 (not_14_out, rom_1_data[4]);
  not not_15 (not_15_out, rom_1_data[3]);
  not not_16 (not_16_out, rom_1_data[2]);
  not not_17 (not_17_out, rom_1_data[1]);
  and to_reg0 (to_reg0_out, not_13_out, not_14_out, not_15_out, not_16_out, not_17_out, rom_1_data[0]);
  and and_1 (and_1_out, cpy_out, to_reg0_out);
  not not_18 (not_18_out, rom_1_data[14]);
  not not_19 (not_19_out, rom_1_data[12]);
  not not_20 (not_20_out, rom_1_data[13]);
  and gto (gto_out, not_12_out, rom_1_data[13], not_18_out, rom_1_data[15]);
  and rst (rst_out, not_19_out, not_20_out, rom_1_data[14], rom_1_data[15]);
  not not_21 (not_21_out, rom_1_data[5]);
  not not_22 (not_22_out, rom_1_data[4]);
  not not_23 (not_23_out, rom_1_data[3]);
  not not_24 (not_24_out, rom_1_data[2]);
  and to_reg1 (to_reg1_out, not_21_out, not_22_out, not_23_out, not_24_out, rom_1_data[1], not_25_out);
  and and_2 (and_2_out, cpy_out, to_reg1_out);
  and hlt (hlt_out, rom_1_data[12], rom_1_data[13], rom_1_data[14], rom_1_data[15]);
  not not_25 (not_25_out, rom_1_data[0]);
  not not_26 (not_26_out, rom_1_data[5]);
  not not_27 (not_27_out, rom_1_data[4]);
  not not_28 (not_28_out, rom_1_data[3]);
  not not_29 (not_29_out, rom_1_data[1]);
  and to_reg2 (to_reg2_out, not_26_out, not_27_out, not_28_out, rom_1_data[2], not_29_out, not_31_out);
  and and_3 (and_3_out, cpy_out, to_reg2_out);
  not not_30 (not_30_out, clc_out);
  or or_1 (or_1_out, clc_out, and_10_out);
  not not_31 (not_31_out, rom_1_data[0]);
  not not_32 (not_32_out, rom_1_data[5]);
  not not_33 (not_33_out, rom_1_data[4]);
  not not_34 (not_34_out, rom_1_data[2]);
  not not_35 (not_35_out, rom_1_data[1]);
  and to_reg3 (to_reg3_out, not_32_out, not_33_out, rom_1_data[3], not_34_out, not_35_out, not_37_out);
  and and_4 (and_4_out, cpy_out, to_reg3_out);
  not not_36 (not_36_out, imm_out);
  Register #(.width(16)) reg0 (
    .D(multiplexer_3_out), .en(multiplexer_1_out), .clk(controlled_buffer_1_out), .Q(reg0_q));  // open: clr
  Register #(.width(16)) reg1 (
    .D(multiplexer_3_out), .en(and_2_out), .clk(controlled_buffer_1_out), .Q(reg1_q));  // open: clr
  Register #(.width(16)) reg2 (
    .D(multiplexer_3_out), .en(and_3_out), .clk(controlled_buffer_1_out), .Q(reg2_q));  // open: clr
  Register #(.width(16)) reg3 (
    .D(multiplexer_3_out), .en(and_4_out), .clk(controlled_buffer_1_out), .Q(reg3_q));  // open: clr
  Register #(.width(16)) reg4 (
    .D(multiplexer_3_out), .en(and_5_out), .clk(controlled_buffer_1_out), .Q(reg4_q));  // open: clr
  Register #(.width(16)) reg5 (
    .D(multiplexer_3_out), .en(and_6_out), .clk(controlled_buffer_1_out), .Q(reg5_q));  // open: clr
  Register #(.width(16)) reg6 (
    .D(multiplexer_3_out), .en(and_7_out), .clk(controlled_buffer_1_out), .Q(reg6_q));  // open: clr
  Register #(.width(16)) alu0 (
    .D(multiplexer_3_out), .en(and_8_out), .clk(controlled_buffer_1_out), .Q(alu0_q));  // open: clr
  Register #(.width(16)) alu1 (
    .D(multiplexer_3_out), .en(and_9_out), .clk(controlled_buffer_1_out), .Q(alu1_q));  // open: clr
  Register #(.width(16)) alu2 (
    .D(multiplexer_2_out), .en(or_1_out), .clk(controlled_buffer_1_out), .Q(alu2_q));  // open: clr
  Multiplexer #(.width(16)) multiplexer_2 (
    .in0(multiplexer_5_out), .in1(multiplexer_3_out), .out(multiplexer_2_out), .sel(not_30_out));
  Register #(.width(16)) out0 (
    .D(multiplexer_3_out), .en(and_11_out), .clk(controlled_buffer_1_out), .Q(out0_q));  // open: clr
  not not_37 (not_37_out, rom_1_data[0]);
  not not_38 (not_38_out, rom_1_data[5]);
  not not_39 (not_39_out, rom_1_data[3]);
  not not_40 (not_40_out, rom_1_data[2]);
  not not_41 (not_41_out, rom_1_data[1]);
  and to_reg4 (to_reg4_out, not_38_out, rom_1_data[4], not_39_out, not_40_out, not_41_out, not_42_out);
  and and_5 (and_5_out, cpy_out, to_reg4_out);
  Multiplexer #(.width(16)) multiplexer_3 (
    .in0(rom_1_data), .in1(multiplexer_4_out), .out(multiplexer_3_out), .sel(not_36_out));
  not not_42 (not_42_out, rom_1_data[0]);
  not not_43 (not_43_out, rom_1_data[4]);
  not not_44 (not_44_out, rom_1_data[3]);
  not not_45 (not_45_out, rom_1_data[2]);
  not not_46 (not_46_out, rom_1_data[1]);
  and to_reg5 (to_reg5_out, rom_1_data[5], not_43_out, not_44_out, not_45_out, not_46_out, not_47_out);
  and and_6 (and_6_out, cpy_out, to_reg5_out);
  not not_47 (not_47_out, rom_1_data[0]);
  not not_48 (not_48_out, rom_1_data[5]);
  not not_49 (not_49_out, rom_1_data[4]);
  not not_50 (not_50_out, rom_1_data[3]);
  not not_51 (not_51_out, rom_1_data[2]);
  and to_reg6 (to_reg6_out, not_48_out, not_49_out, not_50_out, not_51_out, rom_1_data[1], rom_1_data[0]);
  and and_7 (and_7_out, cpy_out, to_reg6_out);
  Multiplexer #(.select(4), .width(16)) multiplexer_4 (
    .in0(reg0_q), .in1(reg1_q), .in2(reg2_q), .in3(reg3_q), .in4(reg4_q), .in5(reg5_q), .in6(reg6_q),
    .in7(alu0_q), .in8(alu1_q), .in9(alu2_q), .in10(out0_q), .out(multiplexer_4_out), .sel(or_2_out));  // open: in11, in12, in13, in14, in15
  not not_52 (not_52_out, rom_1_data[5]);
  not not_53 (not_53_out, rom_1_data[4]);
  not not_54 (not_54_out, rom_1_data[3]);
  and to_alu0 (to_alu0_out, not_52_out, not_53_out, not_54_out, rom_1_data[2], rom_1_data[1], not_55_out);
  and and_8 (and_8_out, cpy_out, to_alu0_out);
  not not_55 (not_55_out, rom_1_data[0]);
  not not_56 (not_56_out, rom_1_data[5]);
  not not_57 (not_57_out, rom_1_data[4]);
  not not_58 (not_58_out, rom_1_data[1]);
  and to_alu1 (to_alu1_out, not_56_out, not_57_out, rom_1_data[3], rom_1_data[2], not_58_out, not_59_out);
  and and_9 (and_9_out, cpy_out, to_alu1_out);
  not not_59 (not_59_out, rom_1_data[0]);
  not not_60 (not_60_out, rom_1_data[5]);
  not not_61 (not_61_out, rom_1_data[2]);
  not not_62 (not_62_out, rom_1_data[1]);
  and to_alu2 (to_alu2_out, not_60_out, rom_1_data[4], rom_1_data[3], not_61_out, not_62_out, not_63_out);
  and and_10 (and_10_out, cpy_out, to_alu2_out);
  not not_63 (not_63_out, rom_1_data[0]);
  and to_out0 (to_out0_out, rom_1_data[5], rom_1_data[4], rom_1_data[3], rom_1_data[2], rom_1_data[1], rom_1_data[0]);
  and and_11 (and_11_out, cpy_out, to_out0_out);
  not not_64 (not_64_out, rom_1_data[11]);
  not not_65 (not_65_out, rom_1_data[10]);
  not not_66 (not_66_out, rom_1_data[9]);
  not not_67 (not_67_out, rom_1_data[8]);
  not not_68 (not_68_out, rom_1_data[7]);
  // AND_Gate from_reg0 has open pins: in0=not_64_out, in1=not_65_out, in2=not_66_out, in3=not_67_out, in4=not_68_out, in5=rom_1_data[6], out=open
  or or_2 (or_2_out[0], from_reg1_out, from_reg3_out, from_alu2_out, from_reg5_out, from_alu0_out);
  not not_69 (not_69_out, rom_1_data[11]);
  not not_70 (not_70_out, rom_1_data[10]);
  not not_71 (not_71_out, rom_1_data[9]);
  not not_72 (not_72_out, rom_1_data[8]);
  and from_reg1 (from_reg1_out, not_69_out, not_70_out, not_71_out, not_72_out, rom_1_data[7], not_73_out);
  or or_3 (or_2_out[1], from_reg2_out, from_reg3_out, from_out0_out, from_reg6_out, from_alu0_out);
  not not_73 (not_73_out, rom_1_data[6]);
  not not_74 (not_74_out, rom_1_data[11]);
  or or_4 (or_2_out[2], from_reg4_out, from_reg5_out, from_reg6_out, from_alu0_out);
  not not_75 (not_75_out, rom_1_data[10]);
  not not_76 (not_76_out, rom_1_data[9]);
  not not_77 (not_77_out, rom_1_data[7]);
  not not_78 (not_78_out, rom_1_data[6]);
  and from_reg2 (from_reg2_out, not_74_out, not_75_out, not_76_out, rom_1_data[8], not_77_out, not_78_out);
  or or_5 (or_2_out[3], from_alu2_out, from_alu1_out, from_out0_out);
  not not_79 (not_79_out, rom_1_data[11]);
  not not_80 (not_80_out, rom_1_data[10]);
  not not_81 (not_81_out, rom_1_data[8]);
  and from_reg3 (from_reg3_out, not_79_out, not_80_out, rom_1_data[9], not_81_out, not_82_out, not_83_out);
  xor xor_1 (xor_1_out, alu0_q[0], alu1_q[0]);
  and and_12 (and_12_out, alu0_q[0], alu1_q[0]);
  and and_13 (and_13_out, alu0_q[0], 1'b0);
  and and_14 (and_14_out, alu1_q[0], 1'b0);
  xor xor_2 (xor_2_out, alu0_q[1], alu1_q[1]);
  and and_15 (and_15_out, alu0_q[1], alu1_q[1]);
  and and_16 (and_16_out, alu0_q[1], carry1_out);
  and and_17 (and_17_out, alu1_q[1], carry1_out);
  xor xor_3 (xor_3_out, alu0_q[2], alu1_q[2]);
  and and_18 (and_18_out, alu0_q[2], alu1_q[2]);
  and and_19 (and_19_out, alu0_q[2], carry2_out);
  and and_20 (and_20_out, alu1_q[2], carry2_out);
  xor xor_4 (xor_4_out, alu0_q[3], alu1_q[3]);
  and and_21 (and_21_out, alu0_q[3], alu1_q[3]);
  and and_22 (and_22_out, alu0_q[3], carry3_out);
  and and_23 (and_23_out, alu1_q[3], carry3_out);
  xor xor_5 (xor_5_out, alu0_q[4], alu1_q[4]);
  and and_24 (and_24_out, alu0_q[4], alu1_q[4]);
  and and_25 (and_25_out, alu0_q[4], carry4_out);
  and and_26 (and_26_out, alu1_q[4], carry4_out);
  xor xor_6 (xor_6_out, alu0_q[5], alu1_q[5]);
  and and_27 (and_27_out, alu0_q[5], alu1_q[5]);
  and and_28 (and_28_out, alu0_q[5], carry5_out);
  and and_29 (and_29_out, alu1_q[5], carry5_out);
  xor xor_7 (xor_7_out, alu0_q[6], alu1_q[6]);
  and and_30 (and_30_out, alu0_q[6], alu1_q[6]);
  and and_31 (and_31_out, alu0_q[6], carry6_out);
  and and_32 (and_32_out, alu1_q[6], carry6_out);
  xor xor_8 (xor_8_out, alu0_q[7], alu1_q[7]);
  and and_33 (and_33_out, alu0_q[7], alu1_q[7]);
  and and_34 (and_34_out, alu0_q[7], carry7_out);
  and and_35 (and_35_out, alu1_q[7], carry7_out);
  xor xor_9 (xor_9_out, alu0_q[8], alu1_q[8]);
  and and_36 (and_36_out, alu0_q[8], alu1_q[8]);
  and and_37 (and_37_out, alu0_q[8], carry8_out);
  and and_38 (and_38_out, alu1_q[8], carry8_out);
  xor xor_10 (xor_10_out, alu0_q[9], alu1_q[9]);
  and and_39 (and_39_out, alu0_q[9], alu1_q[9]);
  and and_40 (and_40_out, alu0_q[9], carry9_out);
  and and_41 (and_41_out, alu1_q[9], carry9_out);
  xor xor_11 (xor_11_out, alu0_q[10], alu1_q[10]);
  and and_42 (and_42_out, alu0_q[10], alu1_q[10]);
  and and_43 (and_43_out, alu0_q[10], carry10_out);
  and and_44 (and_44_out, alu1_q[10], carry10_out);
  xor xor_12 (xor_12_out, alu0_q[11], alu1_q[11]);
  and and_45 (and_45_out, alu0_q[11], alu1_q[11]);
  and and_46 (and_46_out, alu0_q[11], carry11_out);
  and and_47 (and_47_out, alu1_q[11], carry11_out);
  xor xor_13 (xor_13_out, alu0_q[12], alu1_q[12]);
  and and_48 (and_48_out, alu0_q[12], alu1_q[12]);
  and and_49 (and_49_out, alu0_q[12], carry12_out);
  and and_50 (and_50_out, alu1_q[12], carry12_out);
  xor xor_14 (xor_14_out, alu0_q[13], alu1_q[13]);
  and and_51 (and_51_out, alu0_q[13], alu1_q[13]);
  and and_52 (and_52_out, alu0_q[13], carry13_out);
  and and_53 (and_53_out, alu1_q[13], carry13_out);
  xor xor_15 (xor_15_out, alu0_q[14], alu1_q[14]);
  and and_54 (and_54_out, alu0_q[14], alu1_q[14]);
  and and_55 (and_55_out, alu0_q[14], carry14_out);
  and and_56 (and_56_out, alu1_q[14], carry14_out);
  xor xor_16 (xor_16_out, alu0_q[15], alu1_q[15]);
  and and_57 (and_57_out, alu0_q[15], alu1_q[15]);
  and and_58 (and_58_out, alu0_q[15], carry15_out);
  and and_59 (and_59_out, alu1_q[15], carry15_out);
  not not_82 (not_82_out, rom_1_data[7]);
  not not_83 (not_83_out, rom_1_data[6]);
  not not_84 (not_84_out, rom_1_data[11]);
  xor bit1 (bit1_out[0], xor_1_out, 1'b0);
  or carry1 (carry1_out, and_12_out, and_13_out, and_14_out);
  xor bit2 (bit1_out[1], carry1_out, xor_2_out);
  or carry2 (carry2_out, and_15_out, and_16_out, and_17_out);
  xor bit3 (bit1_out[2], carry2_out, xor_3_out);
  or carry3 (carry3_out, and_18_out, and_19_out, and_20_out);
  xor bit4 (bit1_out[3], carry3_out, xor_4_out);
  or carry4 (carry4_out, and_21_out, and_22_out, and_23_out);
  xor bit5 (bit1_out[4], carry4_out, xor_5_out);
  or carry5 (carry5_out, and_24_out, and_25_out, and_26_out);
  xor bit6 (bit1_out[5], carry5_out, xor_6_out);
  or carry6 (carry6_out, and_27_out, and_28_out, and_29_out);
  xor bit7 (bit1_out[6], carry6_out, xor_7_out);
  or carry7 (carry7_out, and_30_out, and_31_out, and_32_out);
  xor bit8 (bit1_out[7], carry7_out, xor_8_out);
  or carry8 (carry8_out, and_33_out, and_34_out, and_35_out);
  xor bit9 (bit1_out[8], carry8_out, xor_9_out);
  or carry9 (carry9_out, and_36_out, and_37_out, and_38_out);
  xor bit10 (bit1_out[9], carry9_out, xor_10_out);
  or carry10 (carry10_out, and_39_out, and_40_out, and_41_out);
  xor bit11 (bit1_out[10], carry10_out, xor_11_out);
  or carry11 (carry11_out, and_42_out, and_43_out, and_44_out);
  xor bit12 (bit1_out[11], carry11_out, xor_12_out);
  or carry12 (carry12_out, and_45_out, and_46_out, and_47_out);
  xor bit13 (bit1_out[12], carry12_out, xor_13_out);
  or carry13 (carry13_out, and_48_out, and_49_out, and_50_out);
  xor bit14 (bit1_out[13], carry13_out, xor_14_out);
  or carry14 (carry14_out, and_51_out, and_52_out, and_53_out);
  xor bit15 (bit1_out[14], carry14_out, xor_15_out);
  or carry15 (carry15_out, and_54_out, and_55_out, and_56_out);
  xor bit16 (bit1_out[15], carry15_out, xor_16_out);
  // OR_Gate carry16 has open pins: in0=and_57_out, in1=and_58_out, in2=and_59_out, out=open
  not not_85 (not_85_out, rom_1_data[9]);
  not not_86 (not_86_out, rom_1_data[8]);
  not not_87 (not_87_out, rom_1_data[7]);
  not not_88 (not_88_out, rom_1_data[6]);
  and from_reg4 (from_reg4_out, not_84_out, rom_1_data[10], not_85_out, not_86_out, not_87_out, not_88_out);
  not not_89 (not_89_out, rom_1_data[10]);
  not not_90 (not_90_out, rom_1_data[9]);
  not not_91 (not_91_out, rom_1_data[8]);
  and from_reg5 (from_reg5_out, rom_1_data[11], not_89_out, not_90_out, not_91_out, not_92_out, not_93_out);
  not not_92 (not_92_out, rom_1_data[7]);
  not not_93 (not_93_out, rom_1_data[6]);
  not not_94 (not_94_out, rom_1_data[11]);
  Multiplexer #(.select(3), .width(16)) multiplexer_5 (
    .in0(bit1_out), .in4(and_60_out), .in5(or_6_out), .in6(nand_1_out), .in7(nor_1_out),
    .out(multiplexer_5_out), .sel(rom_1_data[2:0]));  // open: in1, in2, in3
  not not_95 (not_95_out, rom_1_data[10]);
  not not_96 (not_96_out, rom_1_data[9]);
  not not_97 (not_97_out, rom_1_data[8]);
  and from_reg6 (from_reg6_out, not_94_out, not_95_out, not_96_out, not_97_out, rom_1_data[7], rom_1_data[6]);
  not not_98 (not_98_out, rom_1_data[11]);
  not not_99 (not_99_out, rom_1_data[10]);
  not not_100 (not_100_out, rom_1_data[9]);
  and from_alu0 (from_alu0_out, not_98_out, not_99_out, not_100_out, rom_1_data[8], rom_1_data[7], not_101_out);
  not not_101 (not_101_out, rom_1_data[6]);
  not not_102 (not_102_out, rom_1_data[11]);
  not not_103 (not_103_out, rom_1_data[10]);
  not not_104 (not_104_out, rom_1_data[7]);
  not not_105 (not_105_out, rom_1_data[6]);
  and from_alu1 (from_alu1_out, not_102_out, not_103_out, rom_1_data[9], rom_1_data[8], not_104_out, not_105_out);
  not not_106 (not_106_out, rom_1_data[11]);
  not not_107 (not_107_out, rom_1_data[8]);
  and from_alu2 (from_alu2_out, not_106_out, rom_1_data[10], rom_1_data[9], not_107_out, not_108_out, not_109_out);
  not not_108 (not_108_out, rom_1_data[7]);
  not not_109 (not_109_out, rom_1_data[6]);
  nor nor_1 (nor_1_out[0], alu0_q[0], alu1_q[0]);
  nor nor_2 (nor_1_out[1], alu0_q[1], alu1_q[1]);
  nor nor_3 (nor_1_out[2], alu0_q[2], alu1_q[2]);
  nor nor_4 (nor_1_out[3], alu0_q[3], alu1_q[3]);
  nor nor_5 (nor_1_out[4], alu0_q[4], alu1_q[4]);
  nor nor_6 (nor_1_out[5], alu0_q[5], alu1_q[5]);
  nor nor_7 (nor_1_out[6], alu0_q[6], alu1_q[6]);
  nor nor_8 (nor_1_out[7], alu0_q[7], alu1_q[7]);
  nor nor_9 (nor_1_out[8], alu0_q[8], alu1_q[8]);
  nor nor_10 (nor_1_out[9], alu0_q[9], alu1_q[9]);
  nor nor_11 (nor_1_out[10], alu0_q[10], alu1_q[10]);
  nor nor_12 (nor_1_out[11], alu0_q[11], alu1_q[11]);
  nor nor_13 (nor_1_out[12], alu0_q[12], alu1_q[12]);
  nor nor_14 (nor_1_out[13], alu0_q[13], alu1_q[13]);
  nor nor_15 (nor_1_out[14], alu0_q[14], alu1_q[14]);
  nor nor_16 (nor_1_out[15], alu0_q[15], alu1_q[15]);
  nand nand_1 (nand_1_out[0], alu0_q[0], alu1_q[0]);
  nand nand_2 (nand_1_out[1], alu0_q[1], alu1_q[1]);
  nand nand_3 (nand_1_out[2], alu0_q[2], alu1_q[2]);
  nand nand_4 (nand_1_out[3], alu0_q[3], alu1_q[3]);
  nand nand_5 (nand_1_out[4], alu0_q[4], alu1_q[4]);
  nand nand_6 (nand_1_out[5], alu0_q[5], alu1_q[5]);
  nand nand_7 (nand_1_out[6], alu0_q[6], alu1_q[6]);
  nand nand_8 (nand_1_out[7], alu0_q[7], alu1_q[7]);
  nand nand_9 (nand_1_out[8], alu0_q[8], alu1_q[8]);
  nand nand_10 (nand_1_out[9], alu0_q[9], alu1_q[9]);
  nand nand_11 (nand_1_out[10], alu0_q[10], alu1_q[10]);
  nand nand_12 (nand_1_out[11], alu0_q[11], alu1_q[11]);
  nand nand_13 (nand_1_out[12], alu0_q[12], alu1_q[12]);
  nand nand_14 (nand_1_out[13], alu0_q[13], alu1_q[13]);
  nand nand_15 (nand_1_out[14], alu0_q[14], alu1_q[14]);
  nand nand_16 (nand_1_out[15], alu0_q[15], alu1_q[15]);
  or or_6 (or_6_out[0], alu0_q[0], alu1_q[0]);
  or or_7 (or_6_out[1], alu0_q[1], alu1_q[1]);
  or or_8 (or_6_out[2], alu0_q[2], alu1_q[2]);
  or or_9 (or_6_out[3], alu0_q[3], alu1_q[3]);
  or or_10 (or_6_out[4], alu0_q[4], alu1_q[4]);
  or or_11 (or_6_out[5], alu0_q[5], alu1_q[5]);
  or or_12 (or_6_out[6], alu0_q[6], alu1_q[6]);
  or or_13 (or_6_out[7], alu0_q[7], alu1_q[7]);
  or or_14 (or_6_out[8], alu0_q[8], alu1_q[8]);
  or or_15 (or_6_out[9], alu0_q[9], alu1_q[9]);
  or or_16 (or_6_out[10], alu0_q[10], alu1_q[10]);
  or or_17 (or_6_out[11], alu0_q[11], alu1_q[11]);
  or or_18 (or_6_out[12], alu0_q[12], alu1_q[12]);
  or or_19 (or_6_out[13], alu0_q[13], alu1_q[13]);
  or or_20 (or_6_out[14], alu0_q[14], alu1_q[14]);
  or or_21 (or_6_out[15], alu0_q[15], alu1_q[15]);
  and and_60 (and_60_out[0], alu0_q[0], alu1_q[0]);
  and and_61 (and_60_out[1], alu0_q[1], alu1_q[1]);
  and and_62 (and_60_out[2], alu0_q[2], alu1_q[2]);
  and and_63 (and_60_out[3], alu0_q[3], alu1_q[3]);
  and and_64 (and_60_out[4], alu0_q[4], alu1_q[4]);
  and and_65 (and_60_out[5], alu0_q[5], alu1_q[5]);
  and and_66 (and_60_out[6], alu0_q[6], alu1_q[6]);
  and and_67 (and_60_out[7], alu0_q[7], alu1_q[7]);
  and and_68 (and_60_out[8], alu0_q[8], alu1_q[8]);
  and and_69 (and_60_out[9], alu0_q[9], alu1_q[9]);
  and and_70 (and_60_out[10], alu0_q[10], alu1_q[10]);
  and and_71 (and_60_out[11], alu0_q[11], alu1_q[11]);
  and and_72 (and_60_out[12], alu0_q[12], alu1_q[12]);
  and and_73 (and_60_out[13], alu0_q[13], alu1_q[13]);
  and and_74 (and_60_out[14], alu0_q[14], alu1_q[14]);
  and and_75 (and_60_out[15], alu0_q[15], alu1_q[15]);
  and from_out0 (from_out0_out, rom_1_data[11], rom_1_data[10], rom_1_data[9], rom_1_data[8], rom_1_data[7], rom_1_data[6]);
endmodule
